# Fritzing sketch APP-without led (saved by Fritzing 0.9.3b)
circuit board: 12.5cm x 8cm
breadboards: 1

parts:
  R1 = Resistor [tolerance=±5% resistance=220 package=THT]
  R2 = Resistor [tolerance=±5% resistance=220 package=THT]
  R3 = Resistor [tolerance=±5% resistance=220 package=THT]
  J2 = female pin header, 2 pins [form="♀ (female)"]
  R4 = Resistor [tolerance=±5% resistance=220 package=THT]
  R5 = Resistor [tolerance=±5% resistance=220 package=THT]
  R6 = Resistor [tolerance=±5% resistance=220 package=THT]
  R7 = Resistor [tolerance=±5% resistance=220 package=THT]
  R8 = Resistor [tolerance=±5% resistance=220 package=THT]
  J4 = female pin header, 2 pins [form="♀ (female)"]
  R9 = Resistor [tolerance=±5% resistance=220 package=THT]
  R10 = Resistor [tolerance=±5% resistance=220 package=THT]
  R11 = Resistor [tolerance=±5% resistance=220 package=THT]
  R12 = Resistor [tolerance=±5% resistance=220 package=THT]
  J6 = female pin header, 2 pins [form="♀ (female)"]
  R13 = Resistor [tolerance=±5% resistance=220 package=THT]
  R14 = Resistor [tolerance=±5% resistance=220 package=THT]
  R15 = Resistor [tolerance=±5% resistance=220 package=THT]
  R16 = Resistor [tolerance=±5% resistance=220 package=THT]
  J8 = female pin header, 2 pins [form="♀ (female)"]
  R17 = Resistor [tolerance=±5% resistance=220 package=THT]
  R18 = Resistor [tolerance=±5% resistance=220 package=THT]
  R19 = Resistor [tolerance=±5% resistance=220 package=THT]
  R20 = Resistor [tolerance=±5% resistance=220 package=THT]
  J10 = female pin header, 2 pins [form="♀ (female)"]
  R21 = Resistor [tolerance=±5% resistance=220 package=THT]
  R22 = Resistor [tolerance=±5% resistance=220 package=THT]
  R23 = Resistor [tolerance=±5% resistance=220 package=THT]
  R24 = Resistor [tolerance=±5% resistance=220 package=THT]
  J12 = female pin header, 2 pins [form="♀ (female)"]
  R25 = Resistor [tolerance=±5% resistance=220 package=THT]
  R26 = Resistor [tolerance=±5% resistance=220 package=THT]
  R28 = Resistor [tolerance=±5% resistance=220 package=THT]
  J14 = female pin header, 2 pins [form="♀ (female)"]
  S2 = Pushbutton [package="[THT]"]
  S5 = Pushbutton [package="[THT]"]
  S3 = Pushbutton [package="[THT]"]
  S4 = Pushbutton [package="[THT]"]
  S1 = Pushbutton [package="[THT]"]
  S6 = Pushbutton [package="[THT]"]
  S7 = Pushbutton [package="[THT]"]
  R27 = Resistor [tolerance=±5% resistance=220 package=THT]
  J17 = female pin header, 4 pins [form="♀ (female)"]
  J19 = female pin header, 4 pins [form="♀ (female)"]
  J20 = female pin header, 4 pins [form="♀ (female)"]
  J21 = female pin header, 4 pins [form="♀ (female)"]
  J22 = female pin header, 4 pins [form="♀ (female)"]
  J23 = female pin header, 4 pins [form="♀ (female)"]
  J18 = female pin header, 4 pins [form="♀ (female)"]
  J24 = molex pin header, 2 pins [form=molex]

nets:
  N1: R1.Pin_0, J22.pin1
  N2: R1.Pin_1, R2.Pin_1, R3.Pin_1, R4.Pin_1, R5.Pin_1, R6.Pin_1, R7.Pin_1, R8.Pin_1, R9.Pin_1, R10.Pin_1, R11.Pin_1, R12.Pin_1, R13.Pin_1, R14.Pin_1, R15.Pin_1, R16.Pin_1, R17.Pin_1, R18.Pin_1, R19.Pin_1, R20.Pin_1, R21.Pin_1, R22.Pin_1, R23.Pin_1, R24.Pin_1, R25.Pin_1, R26.Pin_1, R28.Pin_1, R27.Pin_1, J24.pin1
  N3: R2.Pin_0, J22.pin3
  N4: R3.Pin_0, J22.pin4
  N5: J2.pin1, J22.pin2
  N6: J2.pin2, R4.Pin_0, S1.Pin_1, S1.Pin_2
  N7: R5.Pin_0, J23.pin4
  N8: R6.Pin_0, J23.pin2
  N9: R7.Pin_0, J23.pin1
  N10: R8.Pin_0, J4.pin2, S2.Pin_1
  N11: J4.pin1, J23.pin3
  N12: R9.Pin_0, J21.pin1
  N13: R10.Pin_0, J21.pin3
  N14: R11.Pin_0, J21.pin4
  N15: R12.Pin_0, J6.pin2, S3.Pin_1
  N16: J6.pin1, J21.pin2
  N17: R13.Pin_0, J8.pin2, S4.Pin_1
  N18: R14.Pin_0, J20.pin1
  N19: R15.Pin_0, J20.pin4
  N20: R16.Pin_0, J20.pin2
  N21: J8.pin1, J20.pin3
  N22: R17.Pin_0, J19.pin4
  N23: R18.Pin_0, J19.pin1
  N24: R19.Pin_0, J10.pin2, S5.Pin_1, S5.Pin_2
  N25: R20.Pin_0, J19.pin3
  N26: J10.pin1, J19.pin2
  N27: R21.Pin_0, J12.pin2, S6.Pin_1, S6.Pin_2
  N28: R22.Pin_0, J18.pin4
  N29: R23.Pin_0, J18.pin1
  N30: R24.Pin_0, J18.pin2
  N31: J12.pin1, J18.pin3
  N32: R25.Pin_0, J17.pin2
  N33: R26.Pin_0, J17.pin1
  N34: R28.Pin_0, J14.pin2, S7.Pin_1
  N35: J14.pin1, J17.pin3
  N36: S2.Pin_3, S5.Pin_3, S5.Pin_4, S3.Pin_3, S4.Pin_3, S1.Pin_3, S1.Pin_4, S6.Pin_3, S6.Pin_4, S7.Pin_3, J24.pin2
  N37: R27.Pin_0, J17.pin4
