# Fritzing sketch APP (saved by Fritzing 0.9.3b)
circuit board: 18.434cm x 13.877cm
breadboards: 1

parts:
  LED1 = RGB LED (com. anode, rbg) [package="5 mm [THT]"]
  R1 = Resistor [tolerance=±5% resistance=220 package=THT]
  R2 = Resistor [tolerance=±5% resistance=220 package=THT]
  R3 = Resistor [tolerance=±5% resistance=220 package=THT]
  J2 = female pin header, 2 pins [form="♀ (female)"]
  R4 = Resistor [tolerance=±5% resistance=220 package=THT]
  J3 = Screw terminal - 2 pins [package=THT]
  LED2 = RGB LED (com. anode, rbg) [package="5 mm [THT]"]
  R5 = Resistor [tolerance=±5% resistance=220 package=THT]
  R6 = Resistor [tolerance=±5% resistance=220 package=THT]
  R7 = Resistor [tolerance=±5% resistance=220 package=THT]
  R8 = Resistor [tolerance=±5% resistance=220 package=THT]
  J4 = female pin header, 2 pins [form="♀ (female)"]
  LED3 = RGB LED (com. anode, rbg) [package="5 mm [THT]"]
  R9 = Resistor [tolerance=±5% resistance=220 package=THT]
  R10 = Resistor [tolerance=±5% resistance=220 package=THT]
  R11 = Resistor [tolerance=±5% resistance=220 package=THT]
  R12 = Resistor [tolerance=±5% resistance=220 package=THT]
  J6 = female pin header, 2 pins [form="♀ (female)"]
  J7 = Screw terminal - 2 pins [package=THT]
  R13 = Resistor [tolerance=±5% resistance=220 package=THT]
  R14 = Resistor [tolerance=±5% resistance=220 package=THT]
  R15 = Resistor [tolerance=±5% resistance=220 package=THT]
  R16 = Resistor [tolerance=±5% resistance=220 package=THT]
  J8 = female pin header, 2 pins [form="♀ (female)"]
  J9 = Screw terminal - 2 pins [package=THT]
  R17 = Resistor [tolerance=±5% resistance=220 package=THT]
  R18 = Resistor [tolerance=±5% resistance=220 package=THT]
  R19 = Resistor [tolerance=±5% resistance=220 package=THT]
  R20 = Resistor [tolerance=±5% resistance=220 package=THT]
  J10 = female pin header, 2 pins [form="♀ (female)"]
  J11 = Screw terminal - 2 pins [package=THT]
  LED6 = RGB LED (com. anode, rbg) [package="5 mm [THT]"]
  R21 = Resistor [tolerance=±5% resistance=220 package=THT]
  R22 = Resistor [tolerance=±5% resistance=220 package=THT]
  R23 = Resistor [tolerance=±5% resistance=220 package=THT]
  R24 = Resistor [tolerance=±5% resistance=220 package=THT]
  J12 = female pin header, 2 pins [form="♀ (female)"]
  J13 = Screw terminal - 2 pins [package=THT]
  LED7 = RGB LED (com. anode, rbg) [package="5 mm [THT]"]
  R25 = Resistor [tolerance=±5% resistance=220 package=THT]
  R26 = Resistor [tolerance=±5% resistance=220 package=THT]
  R28 = Resistor [tolerance=±5% resistance=220 package=THT]
  J14 = female pin header, 2 pins [form="♀ (female)"]
  J15 = Screw terminal - 2 pins [package=THT]
  S2 = Pushbutton [package="[THT]"]
  S5 = Pushbutton [package="[THT]"]
  S3 = Pushbutton [package="[THT]"]
  S4 = Pushbutton [package="[THT]"]
  S1 = Pushbutton [package="[THT]"]
  S6 = Pushbutton [package="[THT]"]
  S7 = Pushbutton [package="[THT]"]
  J5 = Screw terminal - 2 pins [package=THT]
  J16 = screw terminal, 2 pins
  R27 = Resistor [tolerance=±5% resistance=220 package=THT]
  LED5 = RGB LED (com. anode, rbg) [package="5 mm [THT]"]  # not connected
  LED4 = RGB LED (com. anode, rbg) [package="5 mm [THT]"]

nets:
  N1: LED1.red_cathode, R1.Pin_0
  N2: LED1.common_anode, J2.pin1
  N3: LED1.blue_cathode, R2.Pin_0
  N4: LED1.green_cathode, R3.Pin_0
  N5: R1.Pin_1, R2.Pin_1, R3.Pin_1, R4.Pin_1, J3.pin2, R5.Pin_1, R6.Pin_1, R7.Pin_1, R8.Pin_1, R9.Pin_1, R10.Pin_1, R11.Pin_1, R12.Pin_1, J7.pin2, R13.Pin_1, R14.Pin_1, R15.Pin_1, R16.Pin_1, J9.pin2, R21.Pin_1, R22.Pin_1, R23.Pin_1, R24.Pin_1, J13.pin2, R25.Pin_1, R26.Pin_1, R28.Pin_1, J15.pin2, J5.pin2, J16.pin2, R27.Pin_1
  N6: J2.pin2, R4.Pin_0, S1.Pin_1, S1.Pin_2
  N7: J3.pin1, J7.pin1, J9.pin1, J11.pin1, J13.pin1, J15.pin1, S2.Pin_3, S5.Pin_3, S3.Pin_3, S4.Pin_3, S1.Pin_3, S1.Pin_4, S6.Pin_3, S6.Pin_4, S7.Pin_3, J5.pin1, J16.pin1
  N8: LED2.red_cathode, R5.Pin_0
  N9: LED2.common_anode, J4.pin1
  N10: LED2.blue_cathode, R6.Pin_0
  N11: LED2.green_cathode, R7.Pin_0
  N12: R8.Pin_0, J4.pin2, S2.Pin_1
  N13: LED3.red_cathode, R9.Pin_0
  N14: LED3.common_anode, J6.pin1
  N15: LED3.blue_cathode, R10.Pin_0
  N16: LED3.green_cathode, R11.Pin_0
  N17: R12.Pin_0, J6.pin2, S3.Pin_1
  N18: R13.Pin_0, J8.pin2, S4.Pin_1
  N19: R14.Pin_0, LED4.green_cathode
  N20: R15.Pin_0, LED4.red_cathode
  N21: R16.Pin_0, LED4.blue_cathode
  N22: J8.pin1, LED4.common_anode
  N23: R17.Pin_1, R18.Pin_1, R19.Pin_1, R20.Pin_1, J11.pin2
  N24: R19.Pin_0, J10.pin2, S5.Pin_1
  N25: LED6.red_cathode, R22.Pin_0
  N26: LED6.common_anode, J12.pin1
  N27: LED6.blue_cathode, R24.Pin_0
  N28: LED6.green_cathode, R23.Pin_0
  N29: R21.Pin_0, J12.pin2, S6.Pin_1
  N30: LED7.red_cathode, R27.Pin_0
  N31: LED7.common_anode, J14.pin1
  N32: LED7.blue_cathode, R25.Pin_0
  N33: LED7.green_cathode, R26.Pin_0
  N34: R28.Pin_0, J14.pin2, S7.Pin_1
